# Fritzing sketch arduino-leds (saved by Fritzing 0.8.3b)

parts:
  Resistor = Resistor [tolerance=±5% resistance=220 package=THT]
  Part1 = Arduino Mega 2560 (Rev3)
  LED1 = LED - 5mm [color="Red (633nm)" package="5 mm [THT]"]
  LED2 = LED - 5mm [color="Red (633nm)" package="5 mm [THT]"]
  Resistor1 = Resistor [tolerance=±5% resistance=220 package=THT]

nets:
  N1: Resistor.Pin_0, LED1.anode
  N2: Resistor.Pin_1, Part1.D13_PWM
  N3: Part1.GND, LED1.cathode
  N4: Part1.D2_PWM, Resistor1.Pin_1
  N5: Part1.5V, LED2.anode
  N6: LED2.cathode, Resistor1.Pin_0
