# Fritzing sketch battery-two-diodes (saved by Fritzing 0.8.3b)

parts:
  D2 = Diode [package=diode-1n4001]
  VCC1 = Battery block 9V
  D1 = Diode [package=diode-1n4001]

nets:
  N1: D2.A, VCC1.+
  N2: D2.C, D1.C
  N3: VCC1.-, D1.A
