# Fritzing sketch pin-high (saved by Fritzing 0.8.3b)

parts:
  Pin = female pin header, 1 pin [form="♀ (female)"]
  R2 = Resistor [tolerance=±5% resistance=1M package=THT]

nets:
  5V: Pin.pin1, R2.Pin_0
  GND: R2.Pin_1
