# Fritzing sketch pin-low (saved by Fritzing 0.8.3b)

parts:
  Pin = female pin header, 1 pin [form="♀ (female)"]
  R1 = Resistor [tolerance=±5% resistance=1M package=THT]

nets:
  GND: Pin.pin1, R1.Pin_1
  5V: R1.Pin_0
